// Logisim project control_logic.circ as structural Verilog: 1 circuit, main circuit control_logic
module control_logic (
  input  [31:0] inst,
  input  BrEq,
  input  BrLt,
  output PCSel,
  output RegWEn,
  output [2:0] ImmSel,
  output BrUn,
  output ASel,
  output BSel,
  output [3:0] ALUSel,
  output MemRW,
  output [1:0] WBSel,
  output CSRSel,
  output CSRWen
);

  wire add, add_mul_sub, demultiplexer_2_out1, demultiplexer_2_out2, demultiplexer_2_out3,
       demultiplexer_2_out4, demultiplexer_2_out5, demultiplexer_2_out6, demultiplexer_2_out7, mul, sub;

  Demultiplexer #(.enable("false"), .select(5)) demultiplexer_1 (
    .out12(RegWEn), .sel(inst[6:2]));  // open: out0, out1, out2, out3, out4, out5, out6, out7, out8, out9, out10, out11, out13, out14, out15, out16, out17, out18, out19, out20, out21, out22, out23, out24, out25, out26, out27, out28, out29, out30, out31, in
  not not_1 (ASel, RegWEn);
  not not_2 (BSel, RegWEn);
  Demultiplexer #(.enable("false"), .select(3)) demultiplexer_2 (
    .out0(add_mul_sub), .out1(demultiplexer_2_out1), .out2(demultiplexer_2_out2),
    .out3(demultiplexer_2_out3), .out4(demultiplexer_2_out4), .out5(demultiplexer_2_out5),
    .out6(demultiplexer_2_out6), .out7(demultiplexer_2_out7), .in(RegWEn), .sel(inst[14:12]));
  not not_3 (PCSel, RegWEn);
  Demultiplexer #(.enable("false"), .select(2)) demultiplexer_3 (
    .out0(add), .out1(mul), .out2(sub), .in(add_mul_sub), .sel({inst[30], inst[25]}));  // open: out3
  not not_4 (MemRW, RegWEn);
  assign WBSel = {{1{1'b0}}, RegWEn};  // Bit_Extender bit_extender_1

  // Other names for the same wires on the sheet: func7low = inst[25]; func7high = inst[30]; R_Type = RegWEn

  // Notes on the sheet:
  //   INPUTS to your circuit
  //   R-Type
  //   DON'T CHANGE THE LOCATIONS OF THE INPUTS AND OUTPUTS!
  //   OUTPUT from your circuit
  //   add/mul/sub
  //   and
  //   sll/mulh
  //   or
  //   slt
  //   srl/sra
  //   mulhu
  //   xor
endmodule
